# Fritzing sketch esp32_s3_pn532_i2c (saved by Fritzing 1.0.6)

parts:
  Composant2 = PN532 Elechouse RFID NFC Module V3
  M1 = ESP32-S3-DevKitC-1-N8R8-v1 [part_number=ESP32-S3-DevKitC-1-N8R8-v1]

nets:
  N1: Composant2.GND, M1.pin_22, M1.pin_23
  N2: Composant2.VCC, M1.pin_1, M1.pin_2
  N3: Composant2.SDA, M1.pin_12
  N4: Composant2.SCL, M1.pin_15
  N5: Composant2.IRQ, M1.pin_26
  N6: Composant2.RSTO, M1.pin_27

custom parts:
  PN532 Elechouse RFID NFC Module V3: NFC is a popular technology in recent years. We often heard this work while smart phone company such as Samsung or HTC introduces their latest high-end phones. Almost all the high-end phone in the market support NFC. Near field communication (NFC) is a set of standards for smart phones and similar devices to establish radio communication with each other by touching them together or bringing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
  ESP32-S3-DevKitC-1-N8R8-v1: ESP32-S3-DevKitC-1-N8R8-v1 This module is 44pins long (2x22) and 11 pins width.
